# Fritzing sketch Untitled Sketch (saved by Fritzing 0.9.3b)
breadboards: 1

parts:
  Parça1 = Arduino Uno (Rev3) - ICSP
  M1 = DC Motor
  M2 = DC Motor
  VCC2 = Battery  # not connected
  VCC3 = Battery  # not connected
  VCC4 = Battery  # not connected
  Parça2 = Arduino Motor Shield
  Parça3 = Bluetooth HC-05 Macho  # not connected
  CONN1 = USB connector [package=THT]  # not connected

nets:
  N1: Parça1.D9_PWM, Parça2.A3
  N2: Parça1.D10_PWM/SS, Parça2.A4
  N3: Parça1.D5_PWM, Parça2.A1
  N4: Parça1.D6_PWM, Parça2.A2
  N5: Parça1.GND, Parça2.OUT4
  N6: M1.pin_1, Parça2.D5
  N7: M1.pin_2, Parça2.D9
  N8: M2.pin_1, Parça2.D7
  N9: M2.pin_2, Parça2.D6

notes:
  Motor sürücü olarak
  L298N kullanılmıştır.
  Hc06 Bluetooth sensörü kullanılmıştır.
